# Fritzing sketch Fritzing diagram (saved by Fritzing 0.9.4)
breadboards: 1

parts:
  Part1 = Arduino Uno (Rev3)
  U1 = MCP4251 [package="DIP14 [THT]"]
  R1 = Resistor [tolerance=±5% resistance=220 package=THT]
  LED1 = LED - 5mm [color="Red (633nm)" package="5 mm [THT]"]
  Part2 = Solar Cell
  Part3 = Current Sensor 5A
  R2 = Temperature Sensor (Thermistor) [thermistor_type=NTC package=THT]
  R3 = Photocell (LDR) [package=THT]
  R4 = Resistor [tolerance=±5% resistance=220 package="2512 [SMD]"]
  R5 = Resistor [tolerance=±5% resistance=220 package="2512 [SMD]"]

nets:
  N1: Part1.A0, R3.pin_0, R5.Pin_1
  N2: Part1.A2, R2.pin_1, R4.Pin_0
  N3: Part1.A4/SDA, U1.P0A, Part2.+, Part3.1, Part3.2, Part3.OUT
  N4: Part1.A5/SCL, U1.P0W
  N5: Part1.D10_PWM/SS, U1.CS
  N6: Part1.D11_PWM/MOSI, U1.SDI
  N7: Part1.D12/MISO, U1.SDO
  N8: Part1.D13/SCK, U1.SCK
  5V: Part1.5V, U1.P1A, U1.SHDN, U1.VDD, Part3.VCC, R2.pin_0, R5.Pin_0
  GND: Part1.GND, U1.VSS, U1.P1B, U1.P0B, Part2.-, Part3.GND, R3.pin_1, R4.Pin_1
  N9: U1.P1W, R1.Pin_1
  N10: R1.Pin_0, LED1.anode

custom parts:
  MCP4251: Dual SPI Digital Potentiometer
